// Logisim project alu.circ as structural Verilog: 1 circuit, main circuit alu
module alu (
  input  [31:0] A,
  input  [31:0] B,
  output [31:0] Result
);

  wire ALUSel_p2, ALUSel_p3, ALUSel_p5;
  wire [3:0] ALUSel;
  wire [31:0] add0;

  // Pinn #(.width(4)) ALUSel: pin names not known; wires that end beside it: ALUSel, ALUSel_p2, ALUSel_p3, ALUSel_p3, ALUSel_p5, ALUSel_p5, ALUSel_p2
  Adder #(.width(32)) adder_1 (.a(A), .b(B), .out(add0));  // open: cin, cout

  // Notes on the sheet:
  //   INPUTS to your circuit
  //   DON'T CHANGE THE LOCATIONS OF THE INPUTS AND OUTPUTS!
  //   OUTPUT from your circuit
endmodule
